// Logisim project register_patryk.circ as structural Verilog: 2 circuits, main circuit Register (16b)
// Register
module Register__16b (
  input  [15:0] D,
  input  C,
  input  reset,
  input  write,
  output [15:0] Q
);

  D_Flip_Flop #(.trigger("falling")) d_ff_1 (
    .clk(C), .D(D[0]), .Q(Q[0]), .en(write), .reset(reset));  // open: Qn, preset
  D_Flip_Flop #(.trigger("falling")) d_ff_2 (
    .clk(C), .D(D[4]), .Q(Q[4]), .en(write), .reset(reset));  // open: Qn, preset
  D_Flip_Flop #(.trigger("falling")) d_ff_3 (
    .clk(C), .D(D[8]), .Q(Q[8]), .en(write), .reset(reset));  // open: Qn, preset
  D_Flip_Flop #(.trigger("falling")) d_ff_4 (
    .clk(C), .D(D[12]), .Q(Q[12]), .en(write), .reset(reset));  // open: Qn, preset
  D_Flip_Flop #(.trigger("falling")) d_ff_5 (
    .clk(C), .D(D[1]), .Q(Q[1]), .en(write), .reset(reset));  // open: Qn, preset
  D_Flip_Flop #(.trigger("falling")) d_ff_6 (
    .clk(C), .D(D[5]), .Q(Q[5]), .en(write), .reset(reset));  // open: Qn, preset
  D_Flip_Flop #(.trigger("falling")) d_ff_7 (
    .clk(C), .D(D[9]), .Q(Q[9]), .en(write), .reset(reset));  // open: Qn, preset
  D_Flip_Flop #(.trigger("falling")) d_ff_8 (
    .clk(C), .D(D[13]), .Q(Q[13]), .en(write), .reset(reset));  // open: Qn, preset
  D_Flip_Flop #(.trigger("falling")) d_ff_9 (
    .clk(C), .D(D[2]), .Q(Q[2]), .en(write), .reset(reset));  // open: Qn, preset
  D_Flip_Flop #(.trigger("falling")) d_ff_10 (
    .clk(C), .D(D[6]), .Q(Q[6]), .en(write), .reset(reset));  // open: Qn, preset
  D_Flip_Flop #(.trigger("falling")) d_ff_11 (
    .clk(C), .D(D[10]), .Q(Q[10]), .en(write), .reset(reset));  // open: Qn, preset
  D_Flip_Flop #(.trigger("falling")) d_ff_12 (
    .clk(C), .D(D[14]), .Q(Q[14]), .en(write), .reset(reset));  // open: Qn, preset
  D_Flip_Flop #(.trigger("falling")) d_ff_13 (
    .clk(C), .D(D[3]), .Q(Q[3]), .en(write), .reset(reset));  // open: Qn, preset
  D_Flip_Flop #(.trigger("falling")) d_ff_14 (
    .clk(C), .D(D[7]), .Q(Q[7]), .en(write), .reset(reset));  // open: Qn, preset
  D_Flip_Flop #(.trigger("falling")) d_ff_15 (
    .clk(C), .D(D[11]), .Q(Q[11]), .en(write), .reset(reset));  // open: Qn, preset
  D_Flip_Flop #(.trigger("falling")) d_ff_16 (
    .clk(C), .D(D[15]), .Q(Q[15]), .en(write), .reset(reset));  // open: Qn, preset
endmodule

// Register File
module Register_File__8x16b (
  input  [2:0] rs,
  input  [2:0] rt,
  input  [2:0] rd,
  input  write,
  input  reset,
  input  C,
  input  [15:0] Data,
  output [15:0] S,
  output [15:0] T
);

  wire and_1_out, and_2_out, and_3_out, and_4_out, and_5_out, and_6_out, and_7_out, decoder_1_out1,
       decoder_1_out2, decoder_1_out3, decoder_1_out4, decoder_1_out5, decoder_1_out6, decoder_1_out7;
  wire [15:0] register_16b_1_q, register_16b_2_q, register_16b_3_q, register_16b_4_q, register_16b_5_q,
       register_16b_6_q, register_16b_7_q, zero_q;

  Decoder #(.select(3), .enable("false")) decoder_1 (
    .out1(decoder_1_out1), .out2(decoder_1_out2), .out3(decoder_1_out3), .out4(decoder_1_out4),
    .out5(decoder_1_out5), .out6(decoder_1_out6), .out7(decoder_1_out7), .sel(rd));  // open: out0
  and and_1 (and_1_out, write, decoder_1_out1);
  and and_2 (and_2_out, write, decoder_1_out2);
  and and_3 (and_3_out, write, decoder_1_out3);
  and and_4 (and_4_out, write, decoder_1_out4);
  and and_5 (and_5_out, write, decoder_1_out5);
  and and_6 (and_6_out, write, decoder_1_out6);
  and and_7 (and_7_out, write, decoder_1_out7);
  Register__16b zero (.reset(1'b0), .write(1'b0), .C(C), .D({16{1'b0}}), .Q(zero_q));
  Register__16b register_16b_1 (.reset(reset), .write(and_1_out), .C(C), .D(Data), .Q(register_16b_1_q));
  Register__16b register_16b_2 (.reset(reset), .write(and_2_out), .C(C), .D(Data), .Q(register_16b_2_q));
  Register__16b register_16b_3 (.reset(reset), .write(and_3_out), .C(C), .D(Data), .Q(register_16b_3_q));
  Register__16b register_16b_4 (.reset(reset), .write(and_4_out), .C(C), .D(Data), .Q(register_16b_4_q));
  Register__16b register_16b_5 (.reset(reset), .write(and_5_out), .C(C), .D(Data), .Q(register_16b_5_q));
  Register__16b register_16b_6 (.reset(reset), .write(and_6_out), .C(C), .D(Data), .Q(register_16b_6_q));
  Register__16b register_16b_7 (.reset(reset), .write(and_7_out), .C(C), .D(Data), .Q(register_16b_7_q));
  Multiplexer #(.select(3), .width(16), .enable("false")) multiplexer_1 (
    .in0(zero_q), .in1(register_16b_1_q), .in2(register_16b_2_q), .in3(register_16b_3_q),
    .in4(register_16b_4_q), .in5(register_16b_5_q), .in6(register_16b_6_q), .in7(register_16b_7_q), .out(S),
    .sel(rs));
  Multiplexer #(.select(3), .width(16), .enable("false")) multiplexer_2 (
    .in0(zero_q), .in1(register_16b_1_q), .in2(register_16b_2_q), .in3(register_16b_3_q),
    .in4(register_16b_4_q), .in5(register_16b_5_q), .in6(register_16b_6_q), .in7(register_16b_7_q), .out(T),
    .sel(rt));
endmodule
